// Digital circuit part_c.dig as structural Verilog
module part_c (
  input  in_0,
  input  in_1,
  input  in_2,
  output out_0
);

  wire and_1_out, or_1_out;

  or or_1 (or_1_out, in_1, in_2);
  and and_1 (and_1_out, in_0, or_1_out);
  FGNFET fgnfet_1 (.G(and_1_out), .D(1'b1), .S(out_0));
  FGPFET fgpfet_1 (.G(and_1_out), .S(out_0), .D(1'b0));
endmodule

/* Test case part_c_test:
in_0 in_1 in_2 out_0
 0    0    0    0
 0    0    1    0
 0    1    0    0
 0    1    1    0
 1    0    0    0
 1    0    1    1
 1    1    0    1 
 1    1    1    1 
*/
