// Digital circuit lab2_part2.dig as structural Verilog
module lab2_part2 (
  input  in0,
  input  in1,
  input  in2,
  input  in3,
  output seg_a,
  output seg_f,
  output seg_b,
  output seg_g,
  output seg_e,
  output seg_c,
  output seg_d,
  output seg_dp,
  output sign_a,
  output sign_f,
  output sign_b,
  output sign_g,
  output sign_e,
  output sign_c,
  output sign_d,
  output sign_dp
);

  wire _0, _1, _1_t, _2, _2_t, _4, _4_t, _6, _6_t, _7, _7_t, and_5_out, and_6_out, and_14_out, and_15_out,
       and_16_out, not_1_out, not_2_out, not_3_out, not_4_out, not_5_out, not_6_out, not_7_out, not_8_out,
       not_9_out, not_10_out, not_11_out, not_12_out, not_13_out, not_14_out, not_15_out, not_16_out,
       not_17_out, not_18_out, not_19_out, not_20_out, not_21_out, not_22_out, not_23_out, not_24_out,
       not_25_out, not_26_out, not_27_out, not_28_out, not_29_out, not_30_out, not_31_out, not_32_out;

  Seven_Seg seven_seg_1 (.a(1'b0), .b(1'b0), .c(1'b0), .d(1'b0), .e(1'b0), .f(1'b0), .g(in3), .dp(1'b0));
  Seven_Seg seven_seg_2 (.a(seg_a), .b(seg_b), .c(seg_c), .d(seg_d), .e(seg_e), .f(seg_f), .g(seg_g), .dp(1'b0));
  not not_1 (not_1_out, in3);
  not not_2 (not_2_out, in2);
  not not_3 (not_3_out, in1);
  not not_4 (not_4_out, in1);
  not not_5 (not_5_out, in0);
  not not_6 (not_6_out, in3);
  not not_7 (not_7_out, in1);
  not not_8 (not_8_out, in0);
  not not_9 (not_9_out, in2);
  not not_10 (not_10_out, in3);
  not not_11 (not_11_out, in1);
  not not_12 (not_12_out, in2);
  not not_13 (not_13_out, in0);
  not not_14 (not_14_out, in3);
  not not_15 (not_15_out, in0);
  and and_1 (_1, in3, in2, in1, in0);
  and and_2 (_1_t, not_1_out, not_2_out, not_3_out, in0);
  and and_3 (_4, in3, in2, not_4_out, not_5_out);
  and and_4 (_4_t, not_6_out, in2, not_7_out, not_8_out);
  and and_5 (and_5_out, in3, not_9_out, in1, in0);
  and and_6 (and_6_out, not_10_out, in2, not_11_out, in0);
  and and_7 (_6, in3, not_12_out, in1, not_13_out);
  and and_8 (_6_t, not_14_out, in2, in1, not_15_out);
  nor nor_1 (seg_a, _1, _1_t, _4, _4_t);
  nor nor_2 (seg_b, and_5_out, and_6_out, _6, _6_t);
  and and_9 (_7, in3, not_16_out, not_17_out, in0);
  not not_16 (not_16_out, in2);
  not not_17 (not_17_out, in1);
  and and_10 (_7_t, not_18_out, in2, in1, in0);
  not not_18 (not_18_out, in3);
  and and_11 (_2, in3, in2, in1, not_19_out);
  not not_19 (not_19_out, in0);
  and and_12 (_2_t, not_20_out, not_21_out, in1, not_22_out);
  not not_20 (not_20_out, in3);
  not not_21 (not_21_out, in2);
  not not_22 (not_22_out, in0);
  nor nor_3 (seg_d, _1, _4_t, _7, _7_t, _4, _1_t);
  nor nor_4 (seg_c, _2, _2_t);
  nor nor_5 (seg_g, _7, _7_t, _0, _1, _1_t);
  and and_13 (_0, not_23_out, not_24_out, not_25_out, not_26_out);
  not not_23 (not_23_out, in3);
  not not_24 (not_24_out, in2);
  not not_25 (not_25_out, in1);
  not not_26 (not_26_out, in0);
  and and_14 (and_14_out, in3, not_27_out, not_28_out, not_29_out);
  not not_27 (not_27_out, in2);
  not not_28 (not_28_out, in1);
  not not_29 (not_29_out, in0);
  and and_15 (and_15_out, in3, in2, not_30_out, in0);
  not not_30 (not_30_out, in1);
  and and_16 (and_16_out, not_31_out, not_32_out, in1, in0);
  not not_31 (not_31_out, in3);
  not not_32 (not_32_out, in2);
  or or_1 (seg_e, _0, _6, _2, _2_t, _6_t, and_14_out);
  nor nor_6 (seg_f, and_15_out, and_16_out, _2, _1_t, _1, _2_t, _7, _7_t);

  assign seg_dp = 1'b0;
  assign sign_a = 1'b0;
  assign sign_b = 1'b0;
  assign sign_c = 1'b0;
  assign sign_d = 1'b0;
  assign sign_dp = 1'b0;
  assign sign_e = 1'b0;
  assign sign_f = 1'b0;
  assign sign_g = in3;

  // Notes on the sheet:
  //   Interface (do not edit the content inside this box)
  //   Outputs:
  //   Inputs
  //   Sign
  //   Decimal Number
  //   1111 (-1)
  //   0001 (1)
  //   1100 (-4)
  //   0100 (4)
  //   1011 (-5)
  //   0101 (5)
  //   1010 (-6)
  //   0110 (6)
  //   1001 (-7)
  //   0111 (7)
  //   1110 (-2)
  //   0010 (2)
  //   1000 (-8)
  //   0011 (3)
  //   0000 (0)
  //   1101 (-3)
endmodule

/* Test case:
in3 in2 in1 in0  sign_a sign_b sign_c sign_d sign_e sign_f sign_g  seg_a seg_b seg_c seg_d seg_e seg_f seg_g
 0   0   0   0    0      0      0      0      0      0      0       1     1     1     1     1     1     0
*/
