// Digital circuit playWithRegister.dig as structural Verilog
module playWithRegister (
  input  in_1,
  input  in_2,
  input  in_3,
  input  in_4,
  input  clk,
  input  in_6,
  input  A_3,
  input  A_2,
  input  A_1,
  input  A_0,
  input  clk_2,
  input  in_16,
  input  in_17,
  output Ar_1,
  output Ar_2,
  output Ar_3,
  output Ar_0
);

  wire and_1_out;
  wire [3:0] register_2_q;

  and and_1 (and_1_out, in_16, in_17);
  Register #(.Bits(4)) register_1 (.D({A_0, A_1, A_2, A_3}), .C(clk_2), .en(and_1_out), .Q({Ar_3, Ar_2, Ar_1, Ar_0}));
  Seven_Seg_Hex seven_seg_hex_1 (.d({in_4, in_3, in_2, in_1}), .dp(1'b0));
  Register #(.Bits(4)) register_2 (.D({in_4, in_3, in_2, in_1}), .C(clk), .en(in_6), .Q(register_2_q));
  Seven_Seg_Hex seven_seg_hex_2 (.d(register_2_q), .dp(1'b0));

  // Other names for the same wires on the sheet: _0 = Ar_0; _1 = Ar_1; _2 = Ar_2; _3 = Ar_3

  // Notes on the sheet:
  //   This here's the clock input. 
  //   You dont need to set a periodic clock signal to it.
  //   Just setup some values in A. 
  //   Make sure en=1.
  //   Then change clock value from 0 to 1 and observe what happens
  //   This is a splitter merger component. 
  //   It's functionality should be fairly obvious. 
  //   Right click on it to see how I allocated the input and output wires
  //   Design v1
  //   Design v2
  //   And here, I have hooked up the 7 segment HEX display for better readability
endmodule
